# Fritzing sketch dht11_led_nodeMCU (saved by Fritzing 0.9.3b)
breadboards: 1

parts:
  U1 = NodeMCU V1.0
  M1 = Humidity and Temperature Sensor DHT11
  LED1 = smd LED [color="Blue (430nm)" package="1206 [SMD]"]
  R1 = Resistor [tolerance=±5% resistance=220 package=THT]

nets:
  N1: U1.D2, LED1.anode
  N2: U1.D4, M1.Data
  3V3: U1.3V3, M1.Vcc
  GND: U1.GND, M1.GND, R1.Pin_0
  N3: LED1.cathode, R1.Pin_1

custom parts:
  NodeMCU V1.0: ESP8266 based NodeMCU
  Humidity and Temperature Sensor DHT11: Digital relative humidity & temperature sensor DHT11
